# Fritzing sketch city project (saved by Fritzing 1.0.0rc)
breadboards: 3

parts:
  Breadboard4 = Breadboard Split Power
  Breadboard5 = Breadboard Split Power
  A1 = Particle - Photon2
  Neopixel1 = Adafruit RBG Smart Neopixel [package="DIP (Dual Inline) [THT]"]
  Neopixel2 = Adafruit RBG Smart Neopixel [package="DIP (Dual Inline) [THT]"]
  Neopixel3 = Adafruit RBG Smart Neopixel [package="DIP (Dual Inline) [THT]"]
  Neopixel4 = Adafruit RBG Smart Neopixel [package="DIP (Dual Inline) [THT]"]
  S1 = Pushbutton [package="[THT]"]
  R2 = Resistor [tolerance=±5% resistance=220 package="2010 [SMD]"]
  S3 = Pushbutton [package="[THT]"]
  R5 = Resistor [tolerance=±5% resistance=220 package="2010 [SMD]"]
  Q1 = PNP-Transistor [package="TO92 [THT]"]
  R6 = Resistor [tolerance=±5% resistance=1.8 package="2010 [SMD]"]
  R7 = Resistor [tolerance=±5% resistance=3.3 package="2010 [SMD]"]
  Neopixel5 = Adafruit RBG Smart Neopixel [package="DIP (Dual Inline) [THT]"]
  Neopixel6 = Adafruit RBG Smart Neopixel [package="DIP (Dual Inline) [THT]"]
  Neopixel7 = Adafruit RBG Smart Neopixel [package="DIP (Dual Inline) [THT]"]
  Neopixel8 = Adafruit RBG Smart Neopixel [package="DIP (Dual Inline) [THT]"]
  Neopixel9 = Adafruit RBG Smart Neopixel [package="DIP (Dual Inline) [THT]"]
  Neopixel10 = Adafruit RBG Smart Neopixel [package="DIP (Dual Inline) [THT]"]
  Neopixel11 = Adafruit RBG Smart Neopixel [package="DIP (Dual Inline) [THT]"]
  Neopixel12 = Adafruit RBG Smart Neopixel [package="DIP (Dual Inline) [THT]"]
  Neopixel13 = Adafruit RBG Smart Neopixel [package="DIP (Dual Inline) [THT]"]
  Neopixel14 = Adafruit RBG Smart Neopixel [package="DIP (Dual Inline) [THT]"]
  Neopixel15 = Adafruit RBG Smart Neopixel [package="DIP (Dual Inline) [THT]"]
  Neopixel16 = Adafruit RBG Smart Neopixel [package="DIP (Dual Inline) [THT]"]
  Neopixel17 = Adafruit RBG Smart Neopixel [package="DIP (Dual Inline) [THT]"]
  Neopixel18 = Adafruit RBG Smart Neopixel [package="DIP (Dual Inline) [THT]"]
  Neopixel19 = Adafruit RBG Smart Neopixel [package="DIP (Dual Inline) [THT]"]
  Neopixel20 = Adafruit RBG Smart Neopixel [package="DIP (Dual Inline) [THT]"]
  Neopixel21 = Adafruit RBG Smart Neopixel [package="DIP (Dual Inline) [THT]"]
  Neopixel22 = Adafruit RBG Smart Neopixel [package="DIP (Dual Inline) [THT]"]
  Neopixel23 = Adafruit RBG Smart Neopixel [package="DIP (Dual Inline) [THT]"]
  Neopixel24 = Adafruit RBG Smart Neopixel [package="DIP (Dual Inline) [THT]"]
  DFRobot_DFPlayer_Mini1 = DFRobot DFPlayer Mini [part_number=DFR0299]
  SP1 = SPEAKER [package=pcb_mount_speaker]
  R8 = Resistor [tolerance=±5% resistance=220 package="2010 [SMD]"]
  S4 = Pushbutton [package="[THT]"]
  M1 = seeed grove atomizer v1.0
  M2 = seeed grove atomizer v1.0

nets (from the schematic view):
  N1: Breadboard4.pin4Z, Breadboard4.pin20Z, Breadboard4.pin29Z
  N2: Breadboard4.pin6Y, Breadboard4.pin15Y
  N3: Breadboard4.pin17Y, Breadboard4.pin29Y
  N4: Breadboard5.pin3Y, Breadboard5.pin12Y, Breadboard5.pin15Y
  N5: Breadboard5.pin3Z, Breadboard5.pin11Z, Breadboard5.pin29Z
  N6: A1.Pin_2, A1.Pin_31, S1.Pin_1, S1.Pin_2, R2.Pin_1, S3.Pin_1, S3.Pin_2, R5.Pin_1, R8.Pin_1, S4.Pin_1, S4.Pin_2
  GND: A1.Pin_4, A1.Pin_30, A1.Pin_32, R2.Pin_0, R5.Pin_0, Q1.C, R8.Pin_0, M1.GND, M2.GND
  N7: A1.Pin_14, DFRobot_DFPlayer_Mini1.TX
  N8: A1.Pin_15, DFRobot_DFPlayer_Mini1.RX
  N9: A1.Pin_18, S4.Pin_3, S4.Pin_4
  N10: A1.Pin_19, R7.Pin_0
  N11: A1.Pin_21, S3.Pin_3, S3.Pin_4
  N12: A1.Pin_22, M1.EN
  N13: A1.Pin_23, M2.EN
  N14: A1.Pin_25, S1.Pin_3, S1.Pin_4
  N15: A1.Pin_26, R6.Pin_0, DFRobot_DFPlayer_Mini1.VCC
  VCC: Neopixel1.+, Neopixel2.+, Neopixel3.+, Neopixel4.+, Neopixel5.+, Neopixel6.+, Neopixel7.+, Neopixel8.+, Neopixel9.+, Neopixel10.+, Neopixel11.+, Neopixel12.+, Neopixel13.+, Neopixel14.+, Neopixel15.+, Neopixel16.+, Neopixel17.+, Neopixel18.+, Neopixel19.+, Neopixel20.+, Neopixel21.+, Neopixel22.+, Neopixel23.+, Neopixel24.+, M1.VCC, M2.VCC
  N16: Neopixel1.G, Neopixel2.G, Neopixel3.G, Neopixel4.G, Neopixel5.G, Neopixel6.G, Neopixel7.G, Neopixel8.G, Neopixel9.G, Neopixel10.G, Neopixel11.G, Neopixel12.G, Neopixel13.G, Neopixel14.G, Neopixel15.G, Neopixel16.G, Neopixel17.G, Neopixel18.G, Neopixel19.G, Neopixel20.G, Neopixel21.G, Neopixel22.G, Neopixel23.G, Neopixel24.G
  N17: Neopixel1.O, Neopixel2.In
  N18: Neopixel2.O, Neopixel3.In
  N19: Neopixel3.O, Neopixel4.In
  N20: Neopixel4.O, Neopixel5.In
  N21: Q1.E, R6.Pin_1
  N22: Q1.B, R7.Pin_1
  N23: Neopixel5.O, Neopixel6.In
  N24: Neopixel6.O, Neopixel7.In
  N25: Neopixel7.O, Neopixel8.In
  N26: Neopixel8.O, Neopixel9.In
  N27: Neopixel9.O, Neopixel10.In
  N28: Neopixel11.O, Neopixel13.In
  N29: Neopixel12.In, Neopixel13.O
  N30: Neopixel12.O, Neopixel14.In
  N31: Neopixel14.O, Neopixel15.In
  N32: Neopixel15.O, Neopixel16.In
  N33: Neopixel16.O, Neopixel17.In
  N34: Neopixel17.O, Neopixel22.In
  N35: Neopixel18.In, Neopixel23.O
  N36: Neopixel18.O, Neopixel21.In
  N37: Neopixel19.In, Neopixel24.O
  N38: Neopixel20.In, Neopixel21.O
  N39: Neopixel20.O, Neopixel24.In
  N40: Neopixel22.O, Neopixel23.In
  N41: DFRobot_DFPlayer_Mini1.SPK_1, SP1.-
  N42: DFRobot_DFPlayer_Mini1.GND-1, DFRobot_DFPlayer_Mini1.GND-2
  N43: DFRobot_DFPlayer_Mini1.SPK_2, SP1.+

custom parts:
  Breadboard Split Power: A custom 6 pin per group power supply strip where the top row (ground) is all bussed together and the bottom row (+V) is split in two groups of 12 pins. This version is modified to be a loadable part and was rescaled to be on the standard 1px = 1thou grid with the size set in inches
  Particle - Photon2: The Photon 2 is a microcontroller and Wi-Fi networking developed by particle. Features: 802.11a/b/g/n Wi-Fi, 2.4 GHz and 5 GHz Integrated PCB antenna Integrated U.FL connector for external antenna Integrated RF switch BLE 5 using same antenna as Wi-Fi Realtek RTL8721DM MCU ARM Cortex M33 CPU, 200 MHz 2048 KB (2 MB) user application maximum size 3072 KB (3 MB) of RAM available to user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
  Pushbutton: A generic pushbutton.
  seeed grove atomizer v1.0: Grove - Water Atomization is a perfect module for you to quickly DIY a humidifier with Arduino. You can also develop more advanced and interesting projects with digital scent technology and any other situations in which atomization required.
